// Logisim project Lab 2 - Copy - Copy.circ as structural Verilog: 1 circuit, main circuit main
module main (
  input  B_prime,
  input  C,
  input  A_prime,
  input  D,
  input  A,
  input  B,
  input  C_2,
  input  D_2,
  output out_9,
  output out_10
);

  wire and_1_out, and_2_out, not_1_out, not_2_out, not_3_out, not_4_out, not_5_out, or_2_out, or_3_out,
       or_4_out;

  not not_1 (not_1_out, B_prime);
  not not_2 (not_2_out, A_prime);
  and and_1 (and_1_out, not_1_out, C);
  and and_2 (and_2_out, not_2_out, D);
  not not_3 (not_3_out, A);
  not not_4 (not_4_out, C_2);
  not not_5 (not_5_out, B);
  or or_1 (out_9, and_1_out, and_2_out);
  or or_2 (or_2_out, not_3_out, C_2);
  or or_3 (or_3_out, not_5_out, not_4_out);
  or or_4 (or_4_out, C_2, D_2);
  and and_3 (out_10, or_2_out, or_3_out, or_4_out);

  // Notes on the sheet:
  //   Product of Sums
  //   Sum of Products
endmodule
